// Logisim project 8-bit CPU.circ as structural Verilog: 7 circuits, main circuit 8-bit CPU
module _8_bit_CPU (
);

  wire Ea, Ealu, Ei, Er, EU, La, Lb, Lm, not_1_out, pc_1_out_4, SU, T, T0, T1, T2, UseRAM, W1, W2, Wr;
  wire [2:0] ir_1_tocon;
  wire [7:0] gpr_1_out_7, gpr_1_out_8, ir_1_address, PC_RAM, RAM_IR;

  // Probe on RAM_IR
  PC pc_1 (.in_2(W1), .out_3(PC_RAM), .Ep(UseRAM), .out_4(pc_1_out_4));
  IR ir_1 (.in_3(RAM_IR), .ToCon(ir_1_tocon), .Address(ir_1_address), .Ei(Ei), .in_1(pc_1_out_4), .in_2(W2));
  // Probe on PC_RAM
  MAR mar_1 (.in_1(ir_1_address), .out_4(PC_RAM), .Clk(T0), .Lm(Lm));
  CON con_1 (
    .in_1(T2), .in_2(T1), .in_3(T0), .in_4(W1), .in_6(ir_1_tocon), .Er(Er), .Ei(Ei), .Use_RAM(UseRAM),
    .Ea(Ea), .Ealu(Ealu), .Wr(Wr), .La(La), .Lb(Lb), .Su(SU), .Eu(EU), .Lm(Lm));  // open: in_5
  not not_1 (not_1_out, Wr);
  RAM ram_1 (.addr(PC_RAM), .data(RAM_IR), .clk(T), .ld(not_1_out));  // open: sel, clr
  // Probe on ir_1_address
  assign RAM_IR = Wr ? ir_1_address : 8'bz;  // Controlled_Buffer controlled_buffer_1
  assign ir_1_address = Er ? RAM_IR : 8'bz;  // Controlled_Buffer controlled_buffer_2
  Clock clock_1 (
    .clock_input_enable(1'b1), .out_4(T), .out_5(T2), .out_6(T1), .out_7(T0), .out_8(W1), .out_9(W2),
    .Clock_selection__1_for_internal_clock__0_for_external_clock(1'b1));  // open: reset
  // Probe on gpr_1_out_7
  // Probe on gpr_1_out_8
  ALU alu_1 (
    .in_1(gpr_1_out_7), .in_2(gpr_1_out_8), .out_7(ir_1_address), .in_3(SU), .in_4(EU), .EN(Ealu));  // open: Complete
  GPR gpr_1 (
    .in_1(ir_1_address), .in_2(La), .in_3(Lb), .in_4(Ea), .in_5(T2), .out_6(ir_1_address),
    .out_7(gpr_1_out_7), .out_8(gpr_1_out_8));
endmodule

module GPR (
  input  [7:0] in_1,
  input  in_2,
  input  in_3,
  input  in_4,
  input  in_5,
  output [7:0] out_6,
  output [7:0] out_7,
  output [7:0] out_8
);

  Register A (.D(in_1), .en(in_2), .Q(out_7), .clk(in_5));  // open: clr
  Register B (.D(in_1), .en(in_3), .Q(out_8), .clk(in_5));  // open: clr
  assign out_6 = in_4 ? out_7 : 8'bz;  // Controlled_Buffer controlled_buffer_1

  // Other names for the same wires on the sheet: AtoALU[7:0] = out_7; AtoBus[7:0] = out_6; BtoALU[7:0] = out_8;
  //   CLK = in_5; EA = in_4; Input[7:0] = in_1; LA = in_2; LB = in_3

  // Notes on the sheet:
  //   GPR (General Purpose Registers)
endmodule

module IR (
  input  in_1,
  input  in_2,
  input  [7:0] in_3,
  input  Ei,
  output [2:0] ToCon,
  output [7:0] Address
);

  wire and_1_out, and_2_out, and_3_out, and_4_out, and_5_out, not_1_out, not_2_out, not_3_out, not_4_out,
       not_5_out, not_6_out, not_7_out, not_8_out, not_9_out, not_10_out;
  wire [2:0] or_3_out;
  wire [3:0] register_1_q;

  Register #(.width(4)) register_1 (
    .D({in_3[4], in_3[5], in_3[6], in_3[7]}), .en(1'b1), .Q(register_1_q), .clk(in_2));  // open: clr
  assign Address = Ei ? {4'b0000, in_3[3:0]} : 8'bz;  // Controlled_Buffer controlled_buffer_1
  not not_1 (not_1_out, register_1_q[3]);
  not not_2 (not_2_out, register_1_q[0]);
  not not_3 (not_3_out, register_1_q[1]);
  not not_4 (not_4_out, register_1_q[3]);
  not not_5 (not_5_out, register_1_q[0]);
  not not_6 (not_6_out, register_1_q[1]);
  not not_7 (not_7_out, register_1_q[0]);
  not not_8 (not_8_out, register_1_q[1]);
  not not_9 (not_9_out, register_1_q[2]);
  and and_1 (and_1_out, register_1_q[0], register_1_q[1], register_1_q[2], register_1_q[3]);
  and and_2 (and_2_out, register_1_q[0], register_1_q[1], register_1_q[2], not_1_out);
  and and_3 (and_3_out, not_2_out, not_3_out, register_1_q[2], not_4_out);
  and and_4 (and_4_out, not_5_out, not_6_out, register_1_q[2], register_1_q[3]);
  and and_5 (and_5_out, not_7_out, not_8_out, not_9_out, register_1_q[3]);
  or or_1 (or_3_out[2], and_1_out, and_2_out);
  or or_2 (or_3_out[1], and_1_out, and_3_out, and_4_out);
  or or_3 (or_3_out[0], and_1_out, and_4_out, and_5_out);
  assign ToCon = in_1 ? 3'b000 : 3'bz;  // Controlled_Buffer controlled_buffer_2
  not not_10 (not_10_out, in_1);
  assign ToCon = not_10_out ? or_3_out : 3'bz;  // Controlled_Buffer controlled_buffer_3

  // Notes on the sheet:
  //   IR (Instruction Register)
endmodule

module PC (
  input  Ep,
  input  in_2,
  output [7:0] out_3,
  output out_4
);

  wire or_1_out;
  wire [7:0] adder_1_out, register_1_q;

  Adder adder_1 (.a(8'h1), .b(register_1_q), .out(adder_1_out));  // open: cin, cout
  assign out_3 = Ep ? adder_1_out : 8'bz;  // Controlled_Buffer controlled_buffer_1
  Register register_1 (.D(adder_1_out), .Q(register_1_q), .clk(in_2));  // open: en, clr
  not not_1 (out_4, or_1_out);
  or or_1 (or_1_out, register_1_q[0], register_1_q[1], register_1_q[2], register_1_q[3], register_1_q[4], register_1_q[5], register_1_q[6], register_1_q[7]);

  // Notes on the sheet:
  //   PC (Program Couter)
endmodule

module CON (
  input  in_1,
  input  in_2,
  input  in_3,
  input  in_4,
  input  in_5,
  input  [2:0] in_6,
  output Er,
  output Ei,
  output Use_RAM,
  output Ea,
  output Ealu,
  output Wr,
  output La,
  output Lb,
  output Su,
  output Eu,
  output Lm
);

  wire and_1_out, and_2_out, and_3_out, and_4_out, and_5_out, and_6_out, and_7_out, and_8_out, and_9_out,
       and_10_out, and_11_out, and_12_out, and_13_out, and_14_out, and_15_out, and_16_out, and_21_out,
       and_22_out, and_23_out, and_24_out, and_25_out, not_1_out, not_2_out, not_3_out, not_4_out, not_5_out,
       not_6_out, not_7_out, not_8_out, not_9_out, not_10_out, not_11_out, not_12_out, not_13_out,
       not_14_out, not_15_out, not_16_out, not_17_out, not_18_out, not_19_out, not_20_out, not_21_out,
       not_22_out, not_23_out, not_24_out, not_25_out, not_26_out, not_27_out, not_28_out, not_29_out,
       not_30_out, not_31_out, not_32_out, not_33_out, not_34_out, not_35_out, not_36_out, not_37_out,
       not_38_out, not_39_out, not_40_out, not_41_out, not_42_out, not_43_out, not_44_out, not_45_out,
       not_46_out, not_47_out, not_48_out, not_49_out, not_50_out, not_51_out, not_52_out, not_53_out,
       not_54_out, not_55_out, not_56_out, not_57_out, not_58_out, not_59_out;

  not not_1 (not_1_out, in_3);
  not not_2 (not_2_out, in_4);
  not not_3 (not_3_out, in_6[1]);
  not not_4 (not_4_out, in_6[0]);
  not not_5 (not_5_out, in_4);
  not not_6 (not_6_out, in_6[2]);
  not not_7 (not_7_out, in_6[1]);
  not not_8 (not_8_out, in_6[0]);
  not not_9 (not_9_out, in_4);
  not not_10 (not_10_out, in_6[2]);
  not not_11 (not_11_out, in_6[2]);
  not not_12 (not_12_out, in_6[1]);
  not not_13 (not_13_out, in_6[0]);
  not not_14 (not_14_out, in_6[1]);
  not not_15 (not_15_out, in_6[0]);
  not not_16 (not_16_out, in_6[1]);
  not not_17 (not_17_out, in_1);
  not not_18 (not_18_out, in_6[2]);
  not not_19 (not_19_out, in_1);
  not not_20 (not_20_out, in_6[1]);
  not not_21 (not_21_out, in_1);
  not not_22 (not_22_out, in_6[0]);
  not not_23 (not_23_out, in_3);
  not not_24 (not_24_out, in_4);
  not not_25 (not_25_out, in_6[1]);
  not not_26 (not_26_out, in_3);
  not not_27 (not_27_out, in_4);
  not not_28 (not_28_out, in_6[0]);
  not not_29 (not_29_out, in_3);
  not not_30 (not_30_out, in_4);
  not not_31 (not_31_out, in_6[1]);
  not not_32 (not_32_out, in_3);
  not not_33 (not_33_out, in_4);
  not not_34 (not_34_out, in_6[0]);
  not not_35 (not_35_out, in_4);
  not not_36 (not_36_out, in_6[2]);
  not not_37 (not_37_out, in_6[1]);
  not not_38 (not_38_out, in_6[0]);
  not not_39 (not_39_out, in_4);
  not not_40 (not_40_out, in_6[2]);
  not not_41 (not_41_out, in_4);
  not not_42 (not_42_out, in_6[0]);
  not not_43 (not_43_out, in_4);
  not not_44 (not_44_out, in_6[1]);
  not not_45 (not_45_out, in_4);
  not not_46 (not_46_out, in_6[1]);
  not not_47 (not_47_out, in_4);
  not not_48 (not_48_out, in_6[0]);
  not not_49 (not_49_out, in_3);
  not not_50 (not_50_out, in_4);
  not not_51 (not_51_out, in_6[1]);
  not not_52 (not_52_out, in_3);
  not not_53 (not_53_out, in_1);
  not not_54 (not_54_out, in_4);
  not not_55 (not_55_out, in_6[2]);
  not not_56 (not_56_out, in_2);
  not not_57 (not_57_out, in_1);
  not not_58 (not_58_out, in_4);
  not not_59 (not_59_out, in_6[2]);
  and and_1 (and_1_out, not_1_out, not_2_out, not_3_out, not_4_out);
  and and_2 (and_2_out, not_5_out, not_6_out, not_7_out, not_8_out);
  and and_3 (and_3_out, not_9_out, not_10_out, in_6[1], in_6[0]);
  and and_4 (and_4_out, in_4, not_11_out);
  and and_5 (and_5_out, in_4, not_12_out);
  and and_6 (and_6_out, in_4, not_13_out);
  and and_7 (and_7_out, in_3, not_14_out, in_6[0]);
  and and_8 (and_8_out, in_3, in_6[1], not_15_out);
  and and_9 (and_9_out, in_3, in_6[2], not_16_out);
  and and_10 (and_10_out, not_17_out, in_4, not_18_out);
  and and_11 (and_11_out, not_19_out, in_4, not_20_out);
  and and_12 (and_12_out, not_21_out, in_4, not_22_out);
  and and_13 (and_13_out, not_23_out, not_24_out, not_25_out, in_6[0]);
  and and_14 (and_14_out, not_26_out, not_27_out, in_6[1], not_28_out);
  and and_15 (and_15_out, not_29_out, not_30_out, not_31_out, in_6[0]);
  and and_16 (and_16_out, not_32_out, not_33_out, in_6[1], not_34_out);
  and and_17 (La, not_35_out, not_36_out, not_37_out, not_38_out);
  and and_18 (Lb, not_39_out, not_40_out, in_6[1], in_6[0]);
  and and_19 (Su, not_41_out, in_6[1], not_42_out);
  and and_20 (Eu, not_43_out, not_44_out, in_6[0]);
  and and_21 (and_21_out, not_45_out, not_46_out, in_6[0]);
  and and_22 (and_22_out, not_47_out, in_6[1], not_48_out);
  and and_23 (and_23_out, not_49_out, not_50_out, in_6[2], not_51_out);
  and and_24 (and_24_out, not_52_out, in_2, not_53_out, not_54_out, not_55_out);
  and and_25 (and_25_out, in_3, not_56_out, not_57_out, not_58_out, not_59_out);
  or or_1 (Er, and_1_out, and_2_out, and_3_out);
  or or_2 (Ei, and_4_out, and_5_out, and_6_out, and_7_out, and_8_out, and_9_out);
  or or_3 (Use_RAM, and_10_out, and_11_out, and_12_out);
  or or_4 (Ealu, and_13_out, and_14_out);
  or or_5 (Wr, and_15_out, and_16_out);
  or or_6 (Lm, and_21_out, and_22_out, and_23_out, and_24_out, and_25_out);

  assign Ea = 1'b0;

  // Other names for the same wires on the sheet: OP[2:0] = in_6; T0 = in_3; T1 = in_2; T2 = in_1; W1 = in_4;
  //   W2 = in_5

  // Notes on the sheet:
  //   CON (Control Unit/Decoder)
endmodule

module MAR (
  input  [7:0] in_1,
  input  Clk,
  input  Lm,
  output [7:0] out_4
);

  wire [7:0] register_1_q;

  // Probe on register_1_q
  Register register_1 (.D(in_1), .Q(register_1_q), .clk(Clk));  // open: en, clr
  assign out_4 = Lm ? register_1_q : 8'bz;  // Controlled_Buffer controlled_buffer_1
endmodule

module what (
  input  T0,
  input  T1,
  input  T2,
  input  W1,
  input  S2,
  input  S1,
  input  S0,
  output Er,
  output Ei,
  output Use_RAM,
  output Ea,
  output Ealu,
  output Wr,
  output La,
  output Lb,
  output Su,
  output Eu,
  output Lm
);

  wire and_1_out, and_2_out, and_3_out, and_4_out, and_5_out, and_6_out, and_7_out, and_8_out, and_9_out,
       and_10_out, and_11_out, and_12_out, and_13_out, and_14_out, and_15_out, and_16_out, and_21_out,
       and_22_out, and_23_out, and_24_out, and_25_out, not_1_out, not_2_out, not_3_out, not_4_out, not_5_out,
       not_6_out, not_7_out, not_8_out, not_9_out, not_10_out, not_11_out, not_12_out, not_13_out,
       not_14_out, not_15_out, not_16_out, not_17_out, not_18_out, not_19_out, not_20_out, not_21_out,
       not_22_out, not_23_out, not_24_out, not_25_out, not_26_out, not_27_out, not_28_out, not_29_out,
       not_30_out, not_31_out, not_32_out, not_33_out, not_34_out, not_35_out, not_36_out, not_37_out,
       not_38_out, not_39_out, not_40_out, not_41_out, not_42_out, not_43_out, not_44_out, not_45_out,
       not_46_out, not_47_out, not_48_out, not_49_out, not_50_out, not_51_out, not_52_out, not_53_out,
       not_54_out, not_55_out, not_56_out, not_57_out, not_58_out, not_59_out;

  not not_1 (not_1_out, T0);
  not not_2 (not_2_out, W1);
  not not_3 (not_3_out, S1);
  not not_4 (not_4_out, S0);
  not not_5 (not_5_out, W1);
  not not_6 (not_6_out, S2);
  not not_7 (not_7_out, S1);
  not not_8 (not_8_out, S0);
  not not_9 (not_9_out, W1);
  not not_10 (not_10_out, S2);
  not not_11 (not_11_out, S2);
  not not_12 (not_12_out, S1);
  not not_13 (not_13_out, S0);
  not not_14 (not_14_out, S1);
  not not_15 (not_15_out, S0);
  not not_16 (not_16_out, S1);
  not not_17 (not_17_out, T2);
  not not_18 (not_18_out, S2);
  not not_19 (not_19_out, T2);
  not not_20 (not_20_out, S1);
  not not_21 (not_21_out, T2);
  not not_22 (not_22_out, S0);
  not not_23 (not_23_out, T0);
  not not_24 (not_24_out, W1);
  not not_25 (not_25_out, S1);
  not not_26 (not_26_out, T0);
  not not_27 (not_27_out, W1);
  not not_28 (not_28_out, S0);
  not not_29 (not_29_out, T0);
  not not_30 (not_30_out, W1);
  not not_31 (not_31_out, S1);
  not not_32 (not_32_out, T0);
  not not_33 (not_33_out, W1);
  not not_34 (not_34_out, S0);
  not not_35 (not_35_out, W1);
  not not_36 (not_36_out, S2);
  not not_37 (not_37_out, S1);
  not not_38 (not_38_out, S0);
  not not_39 (not_39_out, W1);
  not not_40 (not_40_out, S2);
  not not_41 (not_41_out, W1);
  not not_42 (not_42_out, S0);
  not not_43 (not_43_out, W1);
  not not_44 (not_44_out, S1);
  not not_45 (not_45_out, W1);
  not not_46 (not_46_out, S1);
  not not_47 (not_47_out, W1);
  not not_48 (not_48_out, S0);
  not not_49 (not_49_out, T0);
  not not_50 (not_50_out, W1);
  not not_51 (not_51_out, S1);
  not not_52 (not_52_out, T0);
  not not_53 (not_53_out, T2);
  not not_54 (not_54_out, W1);
  not not_55 (not_55_out, S2);
  not not_56 (not_56_out, T1);
  not not_57 (not_57_out, T2);
  not not_58 (not_58_out, W1);
  not not_59 (not_59_out, S2);
  and and_1 (and_1_out, not_1_out, not_2_out, not_3_out, not_4_out);
  and and_2 (and_2_out, not_5_out, not_6_out, not_7_out, not_8_out);
  and and_3 (and_3_out, not_9_out, not_10_out, S1, S0);
  and and_4 (and_4_out, W1, not_11_out);
  and and_5 (and_5_out, W1, not_12_out);
  and and_6 (and_6_out, W1, not_13_out);
  and and_7 (and_7_out, T0, not_14_out, S0);
  and and_8 (and_8_out, T0, S1, not_15_out);
  and and_9 (and_9_out, T0, S2, not_16_out);
  and and_10 (and_10_out, not_17_out, W1, not_18_out);
  and and_11 (and_11_out, not_19_out, W1, not_20_out);
  and and_12 (and_12_out, not_21_out, W1, not_22_out);
  and and_13 (and_13_out, not_23_out, not_24_out, not_25_out, S0);
  and and_14 (and_14_out, not_26_out, not_27_out, S1, not_28_out);
  and and_15 (and_15_out, not_29_out, not_30_out, not_31_out, S0);
  and and_16 (and_16_out, not_32_out, not_33_out, S1, not_34_out);
  and and_17 (La, not_35_out, not_36_out, not_37_out, not_38_out);
  and and_18 (Lb, not_39_out, not_40_out, S1, S0);
  and and_19 (Su, not_41_out, S1, not_42_out);
  and and_20 (Eu, not_43_out, not_44_out, S0);
  and and_21 (and_21_out, not_45_out, not_46_out, S0);
  and and_22 (and_22_out, not_47_out, S1, not_48_out);
  and and_23 (and_23_out, not_49_out, not_50_out, S2, not_51_out);
  and and_24 (and_24_out, not_52_out, T1, not_53_out, not_54_out, not_55_out);
  and and_25 (and_25_out, T0, not_56_out, not_57_out, not_58_out, not_59_out);
  or or_1 (Er, and_1_out, and_2_out, and_3_out);
  or or_2 (Ei, and_4_out, and_5_out, and_6_out, and_7_out, and_8_out, and_9_out);
  or or_3 (Use_RAM, and_10_out, and_11_out, and_12_out);
  or or_4 (Ealu, and_13_out, and_14_out);
  or or_5 (Wr, and_15_out, and_16_out);
  or or_6 (Lm, and_21_out, and_22_out, and_23_out, and_24_out, and_25_out);

  assign Ea = 1'b0;
endmodule
