// Logisim project ALU.circ as structural Verilog: 7 circuits, main circuit ALU
module ALU (
  input  [7:0] in_1,
  input  [7:0] in_2,
  input  in_3,
  input  in_4,
  input  EN,
  output Complete,
  output [7:0] out_7
);

  wire and_1_out, and_2_out, n8_bit_complement_1_out_9, n8_bit_complement_1_out_10,
       n8_bit_complement_1_out_11, n8_bit_complement_1_out_12, n8_bit_complement_1_out_13,
       n8_bit_complement_1_out_14, n8_bit_complement_1_out_15, n8_bit_complement_1_out_16,
       n8_bit_complement_2_out_9, n8_bit_complement_2_out_10, n8_bit_complement_2_out_11,
       n8_bit_complement_2_out_12, n8_bit_complement_2_out_13, n8_bit_complement_2_out_14,
       n8_bit_complement_2_out_15, n8_bit_complement_2_out_16, n8_bit_full_adder_1_s0,
       n8_bit_full_adder_1_s1, n8_bit_full_adder_1_s2, n8_bit_full_adder_1_s3, n8_bit_full_adder_1_s4,
       n8_bit_full_adder_1_s5, n8_bit_full_adder_1_s6, n8_bit_full_adder_1_s7, not_1_out, or_1_out, xor_1_out;
  wire [7:0] n8_bit_complement_3_out_16, n8_bit_or_1_out_24, n8_bit_selector_1_out_4;

  and and_1 (and_1_out, in_3, not_1_out);
  not not_1 (not_1_out, in_4);
  xor xor_1 (xor_1_out, in_2[7], and_1_out);
  _8_bit_complement u_8_bit_complement_1 (
    .in_1(in_1[7]), .in_2(in_1[6]), .in_3(in_1[5]), .in_4(in_1[4]), .in_5(in_1[3]), .in_6(in_1[2]),
    .in_7(in_1[1]), .in_8(in_1[0]), .out_9(n8_bit_complement_1_out_9), .out_10(n8_bit_complement_1_out_10),
    .out_11(n8_bit_complement_1_out_11), .out_12(n8_bit_complement_1_out_12),
    .out_13(n8_bit_complement_1_out_13), .out_14(n8_bit_complement_1_out_14),
    .out_15(n8_bit_complement_1_out_15), .out_16(n8_bit_complement_1_out_16));
  _8_bit_complement u_8_bit_complement_2 (
    .in_1(xor_1_out), .in_2(in_2[6]), .in_3(in_2[5]), .in_4(in_2[4]), .in_5(in_2[3]), .in_6(in_2[2]),
    .in_7(in_2[1]), .in_8(in_2[0]), .out_9(n8_bit_complement_2_out_9), .out_10(n8_bit_complement_2_out_10),
    .out_11(n8_bit_complement_2_out_11), .out_12(n8_bit_complement_2_out_12),
    .out_13(n8_bit_complement_2_out_13), .out_14(n8_bit_complement_2_out_14),
    .out_15(n8_bit_complement_2_out_15), .out_16(n8_bit_complement_2_out_16));
  and and_2 (and_2_out, in_3, in_4);
  _8_bit_full_adder u_8_bit_full_adder_1 (
    .X0(n8_bit_complement_1_out_16), .X4(n8_bit_complement_1_out_12), .Y0(n8_bit_complement_2_out_16),
    .Y4(n8_bit_complement_2_out_12), .X1(n8_bit_complement_1_out_15), .X5(n8_bit_complement_1_out_11),
    .Y1(n8_bit_complement_2_out_15), .Y5(n8_bit_complement_2_out_11), .X2(n8_bit_complement_1_out_14),
    .X6(n8_bit_complement_1_out_10), .Y2(n8_bit_complement_2_out_14), .Y6(n8_bit_complement_2_out_10),
    .X3(n8_bit_complement_1_out_13), .X7(n8_bit_complement_1_out_9), .Y3(n8_bit_complement_2_out_13),
    .Y7(n8_bit_complement_2_out_9), .S0(n8_bit_full_adder_1_s0), .S4(n8_bit_full_adder_1_s4),
    .S1(n8_bit_full_adder_1_s1), .S5(n8_bit_full_adder_1_s5), .S2(n8_bit_full_adder_1_s2),
    .S6(n8_bit_full_adder_1_s6), .S3(n8_bit_full_adder_1_s3), .S7(n8_bit_full_adder_1_s7), .Cin(1'b0));  // open: Cout
  _8_bit_or u_8_bit_or_1 (
    .in_1(n8_bit_complement_1_out_9), .in_2(n8_bit_complement_2_out_9), .in_3(n8_bit_complement_1_out_10),
    .in_4(n8_bit_complement_2_out_10), .in_5(n8_bit_complement_1_out_11), .in_6(n8_bit_complement_2_out_11),
    .in_7(n8_bit_complement_1_out_12), .in_8(n8_bit_complement_2_out_12), .in_9(n8_bit_complement_1_out_13),
    .in_10(n8_bit_complement_2_out_13), .in_11(n8_bit_complement_1_out_14),
    .in_12(n8_bit_complement_2_out_14), .in_13(n8_bit_complement_1_out_15),
    .in_14(n8_bit_complement_2_out_15), .in_15(n8_bit_complement_1_out_16),
    .in_16(n8_bit_complement_2_out_16), .out_17(n8_bit_or_1_out_24[7]), .out_18(n8_bit_or_1_out_24[6]),
    .out_19(n8_bit_or_1_out_24[5]), .out_20(n8_bit_or_1_out_24[4]), .out_21(n8_bit_or_1_out_24[3]),
    .out_22(n8_bit_or_1_out_24[2]), .out_23(n8_bit_or_1_out_24[1]), .out_24(n8_bit_or_1_out_24[0]));
  _8_bit_complement u_8_bit_complement_3 (
    .in_1(n8_bit_full_adder_1_s7), .in_2(n8_bit_full_adder_1_s6), .in_3(n8_bit_full_adder_1_s5),
    .in_4(n8_bit_full_adder_1_s4), .in_5(n8_bit_full_adder_1_s3), .in_6(n8_bit_full_adder_1_s2),
    .in_7(n8_bit_full_adder_1_s1), .in_8(n8_bit_full_adder_1_s0), .out_9(n8_bit_complement_3_out_16[7]),
    .out_10(n8_bit_complement_3_out_16[6]), .out_11(n8_bit_complement_3_out_16[5]),
    .out_12(n8_bit_complement_3_out_16[4]), .out_13(n8_bit_complement_3_out_16[3]),
    .out_14(n8_bit_complement_3_out_16[2]), .out_15(n8_bit_complement_3_out_16[1]),
    .out_16(n8_bit_complement_3_out_16[0]));
  assign out_7 = EN ? n8_bit_selector_1_out_4 : 8'bz;  // Controlled_Buffer controlled_buffer_1
  _8_bit_selector u_8_bit_selector_1 (
    .A(n8_bit_complement_3_out_16), .B(n8_bit_or_1_out_24), .in_3(and_2_out), .out_4(n8_bit_selector_1_out_4));
  or or_1 (or_1_out, n8_bit_selector_1_out_4[7], n8_bit_selector_1_out_4[6], n8_bit_selector_1_out_4[5], n8_bit_selector_1_out_4[4], n8_bit_selector_1_out_4[3], n8_bit_selector_1_out_4[2], n8_bit_selector_1_out_4[1], n8_bit_selector_1_out_4[0]);
  not not_2 (Complete, or_1_out);

  // Notes on the sheet:
  //   To perform subtraction, invert
  //   the first digit of the second number
  //   Find the two's complement of both input numbers.
  //   Use a adder to calculate the sum of two's complements.
  //   Then the result is padded once.
  //   The ALU calculates the results of addition, subtraction, and bitwise OR
  //   operations, and uses a selector to choose which result to output.
endmodule

module _1_bit_full_adder (
  input  A,
  input  B,
  input  Cin,
  output S,
  output Cout
);

  wire and_1_out, and_2_out, xor_1_out;

  xor xor_1 (xor_1_out, A, B);
  xor xor_2 (S, xor_1_out, Cin);
  and and_1 (and_1_out, xor_1_out, Cin);
  and and_2 (and_2_out, A, B);
  or or_1 (Cout, and_1_out, and_2_out);

  // Notes on the sheet:
  //   1-bit full adder
endmodule

module _8_bit_full_adder (
  input  Cin,
  input  X0,
  input  X4,
  input  Y0,
  input  Y4,
  input  X1,
  input  X5,
  input  Y1,
  input  Y5,
  input  X2,
  input  X6,
  input  Y2,
  input  Y6,
  input  X3,
  input  X7,
  input  Y3,
  input  Y7,
  output S0,
  output S4,
  output S1,
  output S5,
  output S2,
  output S6,
  output S3,
  output S7,
  output Cout
);

  wire n1_bit_full_adder_1_cout, n1_bit_full_adder_2_cout, n1_bit_full_adder_3_cout,
       n1_bit_full_adder_4_cout, n1_bit_full_adder_5_cout, n1_bit_full_adder_6_cout, n1_bit_full_adder_7_cout;

  _1_bit_full_adder u_1_bit_full_adder_1 (.A(Y0), .B(X0), .Cin(Cin), .S(S0), .Cout(n1_bit_full_adder_1_cout));
  _1_bit_full_adder u_1_bit_full_adder_2 (
    .A(Y1), .B(X1), .Cin(n1_bit_full_adder_1_cout), .S(S1), .Cout(n1_bit_full_adder_2_cout));
  _1_bit_full_adder u_1_bit_full_adder_3 (
    .A(Y2), .B(X2), .Cin(n1_bit_full_adder_2_cout), .S(S2), .Cout(n1_bit_full_adder_3_cout));
  _1_bit_full_adder u_1_bit_full_adder_4 (
    .A(Y3), .B(X3), .Cin(n1_bit_full_adder_3_cout), .S(S3), .Cout(n1_bit_full_adder_4_cout));
  _1_bit_full_adder u_1_bit_full_adder_5 (
    .A(Y4), .B(X4), .Cin(n1_bit_full_adder_4_cout), .S(S4), .Cout(n1_bit_full_adder_5_cout));
  _1_bit_full_adder u_1_bit_full_adder_6 (
    .A(Y5), .B(X5), .Cin(n1_bit_full_adder_5_cout), .S(S5), .Cout(n1_bit_full_adder_6_cout));
  _1_bit_full_adder u_1_bit_full_adder_7 (
    .A(Y6), .B(X6), .Cin(n1_bit_full_adder_6_cout), .S(S6), .Cout(n1_bit_full_adder_7_cout));
  _1_bit_full_adder u_1_bit_full_adder_8 (.A(Y7), .B(X7), .Cin(n1_bit_full_adder_7_cout), .S(S7), .Cout(Cout));

  // Notes on the sheet:
  //   8-bit full adder
endmodule

module _1_bit_selector (
  input  A,
  input  B,
  input  Select,
  output Result
);

  wire and_1_out, and_2_out, not_1_out;

  not not_1 (not_1_out, Select);
  and and_1 (and_1_out, A, not_1_out);
  and and_2 (and_2_out, B, Select);
  or or_1 (Result, and_1_out, and_2_out);

  // Notes on the sheet:
  //   1-bit selector
endmodule

module _8_bit_selector (
  input  [7:0] A,
  input  [7:0] B,
  input  in_3,
  output [7:0] out_4
);

  _1_bit_selector u_1_bit_selector_1 (.A(A[0]), .B(B[0]), .Select(in_3), .Result(out_4[0]));
  _1_bit_selector u_1_bit_selector_2 (.A(A[1]), .B(B[1]), .Select(in_3), .Result(out_4[1]));
  _1_bit_selector u_1_bit_selector_3 (.A(A[2]), .B(B[2]), .Select(in_3), .Result(out_4[2]));
  _1_bit_selector u_1_bit_selector_4 (.A(A[3]), .B(B[3]), .Select(in_3), .Result(out_4[3]));
  _1_bit_selector u_1_bit_selector_5 (.A(A[4]), .B(B[4]), .Select(in_3), .Result(out_4[4]));
  _1_bit_selector u_1_bit_selector_6 (.A(A[5]), .B(B[5]), .Select(in_3), .Result(out_4[5]));
  _1_bit_selector u_1_bit_selector_7 (.A(A[6]), .B(B[6]), .Select(in_3), .Result(out_4[6]));
  _1_bit_selector u_1_bit_selector_8 (.A(A[7]), .B(B[7]), .Select(in_3), .Result(out_4[7]));

  // Notes on the sheet:
  //   8-bit selector
endmodule

module _8_bit_complement (
  input  in_1,
  input  in_2,
  input  in_3,
  input  in_4,
  input  in_5,
  input  in_6,
  input  in_7,
  input  in_8,
  output out_9,
  output out_10,
  output out_11,
  output out_12,
  output out_13,
  output out_14,
  output out_15,
  output out_16
);

  wire and_1_out, and_2_out, and_3_out, and_4_out, and_5_out, and_6_out, and_7_out, xor_1_out, xor_2_out,
       xor_3_out, xor_4_out, xor_5_out, xor_6_out, xor_7_out;

  xor xor_1 (xor_1_out, in_2, in_1);
  xor xor_2 (xor_2_out, in_3, in_1);
  xor xor_3 (xor_3_out, in_4, in_1);
  xor xor_4 (xor_4_out, in_5, in_1);
  xor xor_5 (xor_5_out, in_6, in_1);
  xor xor_6 (xor_6_out, in_7, in_1);
  xor xor_7 (xor_7_out, in_8, in_1);
  and and_1 (and_1_out, xor_7_out, in_1);
  and and_2 (and_2_out, xor_6_out, and_1_out);
  xor xor_8 (out_16, xor_7_out, in_1);
  and and_3 (and_3_out, xor_5_out, and_2_out);
  xor xor_9 (out_15, xor_6_out, and_1_out);
  and and_4 (and_4_out, xor_4_out, and_3_out);
  xor xor_10 (out_14, xor_5_out, and_2_out);
  and and_5 (and_5_out, xor_3_out, and_4_out);
  xor xor_11 (out_13, xor_4_out, and_3_out);
  and and_6 (and_6_out, xor_2_out, and_5_out);
  xor xor_12 (out_12, xor_3_out, and_4_out);
  and and_7 (and_7_out, xor_1_out, and_6_out);
  xor xor_13 (out_11, xor_2_out, and_5_out);
  xor xor_14 (out_9, in_1, and_7_out);
  xor xor_15 (out_10, xor_1_out, and_6_out);

  // Notes on the sheet:
  //   Find 8-bit complement
endmodule

module _8_bit_or (
  input  in_1,
  input  in_2,
  input  in_3,
  input  in_4,
  input  in_5,
  input  in_6,
  input  in_7,
  input  in_8,
  input  in_9,
  input  in_10,
  input  in_11,
  input  in_12,
  input  in_13,
  input  in_14,
  input  in_15,
  input  in_16,
  output out_17,
  output out_18,
  output out_19,
  output out_20,
  output out_21,
  output out_22,
  output out_23,
  output out_24
);

  or or_1 (out_17, in_1, in_2);
  or or_2 (out_18, in_3, in_4);
  or or_3 (out_19, in_5, in_6);
  or or_4 (out_20, in_7, in_8);
  or or_5 (out_21, in_9, in_10);
  or or_6 (out_22, in_11, in_12);
  or or_7 (out_23, in_13, in_14);
  or or_8 (out_24, in_15, in_16);

  // Notes on the sheet:
  //   8-bit bitwise OR operation
endmodule
