// Logisim project ClockDemo.circ as structural Verilog: 2 circuits, main circuit Clock
module Clock (
  input  reset,
  input  clock_input_enable,
  input  Clock_selection__1_for_internal_clock__0_for_external_clock,
  output out_4,
  output out_5,
  output out_6,
  output out_7,
  output out_8,
  output out_9
);

  wire clk_1_internal_clock_output, clock_input_out;

  Button clock_input (.out(clock_input_out));
  clk clk_1 (
    .ET__Clock_Generation_Enable(clock_input_enable),
    .QD__Generates_a_clock__connected_to_a_button(clock_input_out), .reset(reset), .W2(out_9), .W1(out_8),
    .Internal_clock_output(clk_1_internal_clock_output), .T2__The_third_beat_oof_the_clock(out_5),
    .T1_Second_beat_of_the_clock(out_6), .T0_The_first_beat_of_tthe_clock(out_7),
    .Clock_selection__1__Internal_crystal_clock__0__External_clock_input(Clock_selection__1_for_internal_clock__0_for_external_clock));
  Multiplexer multiplexer_1 (
    .in0(clock_input_out), .in1(clk_1_internal_clock_output), .out(out_4),
    .sel(Clock_selection__1_for_internal_clock__0_for_external_clock));  // open: en

  // Other names for the same wires on the sheet: clk = out_4; T0 = out_7; T1 = out_6; T2 = out_5; W1 = out_8;
  //   W2 = out_9
endmodule

// CLK
module clk (
  input  ET__Clock_Generation_Enable,
  input  QD__Generates_a_clock__connected_to_a_button,
  input  Clock_selection__1__Internal_crystal_clock__0__External_clock_input,
  input  reset,
  output W1,
  output W2,
  output T1_Second_beat_of_the_clock,
  output T0_The_first_beat_of_tthe_clock,
  output T2__The_third_beat_oof_the_clock,
  output Internal_clock_output
);

  wire and_1_out, clock_1_out, counter_2_q, multiplexer_1_out;
  wire [1:0] counter_1_q;

  and and_1 (and_1_out, ET__Clock_Generation_Enable, Clock_selection__1__Internal_crystal_clock__0__External_clock_input);
  Clock_part clock_1 (.out(clock_1_out));
  Multiplexer multiplexer_1 (
    .in0(QD__Generates_a_clock__connected_to_a_button), .in1(clock_1_out), .out(multiplexer_1_out),
    .sel(and_1_out));  // open: en
  assign Internal_clock_output = and_1_out ? clock_1_out : 1'bz;  // Controlled_Buffer controlled_buffer_1
  Counter #(.width(2), .max('h2)) counter_1 (
    .load(1'b0), .count(1'b1), .Q(counter_1_q), .clk(multiplexer_1_out), .clr(reset));  // open: D, carry
  Decoder #(.select(2)) decoder_1 (
    .out0(T2__The_third_beat_oof_the_clock), .out1(T0_The_first_beat_of_tthe_clock),
    .out2(T1_Second_beat_of_the_clock), .sel(counter_1_q), .en(ET__Clock_Generation_Enable));  // open: out3
  Counter #(.width(1), .max('h1)) counter_2 (
    .D(ET__Clock_Generation_Enable), .Q(counter_2_q), .clk(T0_The_first_beat_of_tthe_clock), .clr(reset));  // open: load, count, carry
  Decoder decoder_2 (.out0(W2), .out1(W1), .sel(counter_2_q), .en(ET__Clock_Generation_Enable));

  // Notes on the sheet:
  //   ET__Clock_Generation_Enable: pull=down
endmodule
